# Fritzing sketch PS2ArduinoWiring (saved by Fritzing 0.9.1b)
breadboards: 1

parts:
  Part1 = Arduino Uno (Rev3)
  R1 = Resistor [tolerance=±5% resistance=1k package=THT]
  LED1 = LED - 5mm [color="White (4500K)" package="5 mm [THT]"]
  LED2 = LED - 5mm [color="White (4500K)" package="5 mm [THT]"]
  LED3 = LED - 5mm [color="White (4500K)" package="5 mm [THT]"]
  LED4 = LED - 5mm [color="White (4500K)" package="5 mm [THT]"]
  R2 = Resistor [tolerance=±5% resistance=220 package=THT]
  R3 = Resistor [tolerance=±5% resistance=220 package=THT]
  R4 = Resistor [tolerance=±5% resistance=220 package=THT]
  R5 = Resistor [tolerance=±5% resistance=220 package=THT]

nets:
  N1: Part1.D9_PWM, LED3.anode
  N2: Part1.D12/MISO, R1.Pin_0
  N3: Part1.D3_PWM, LED2.anode
  N4: Part1.D4, LED4.anode
  N5: Part1.D6_PWM, LED1.anode
  N6: Part1.3V3, R1.Pin_1
  N7: Part1.GND, R2.Pin_1, R3.Pin_1, R4.Pin_1, R5.Pin_1
  N8: LED1.cathode, R2.Pin_0
  N9: LED2.cathode, R3.Pin_0
  N10: LED3.cathode, R5.Pin_0
  N11: LED4.cathode, R4.Pin_0

notes:
  1. data 2. command 3. vibration 4. ground 5. VCC power 6. attenuation/ sel 7. clock 8. - 9. -
  PS2 controller with the "SONY" side down and wires directed away. Pins 1,2,4,5,6 and 7 are connected with female - male wires (the female end clicked on the PS2 pins - no stripping needed!)
